// Logisim project lab3.circ as structural Verilog: 5 circuits, main circuit main
module main (
  output [4:0] x0_4
);

  wire [1:0] \подсхема_1_f0_1 , \подсхема_1_f2_1 , \подсхема_2_f0_2 , \подсхема_2_f2_2 , \подсхема_3_f0_3 ,
       \подсхема_3_f2_3 , \подсхема_4_f0_4 , \подсхема_4_f2_4 ;

  podshema1 \u_подсхема_1  (
    .x0_4(5'b00101), .F3_1(\подсхема_1_f2_1 [1]), .F2_1(\подсхема_1_f2_1 [0]), .F1_1(\подсхема_1_f0_1 [1]),
    .F0_1(\подсхема_1_f0_1 [0]));
  podshema2 \u_подсхема_2  (
    .x0_4(5'b00101), .F3_2(\подсхема_2_f2_2 [1]), .F2_2(\подсхема_2_f2_2 [0]), .F1_2(\подсхема_2_f0_2 [1]),
    .F0_2(\подсхема_2_f0_2 [0]));
  podshema3 \u_подсхема_3  (
    .x0_4(5'b00101), .F3_3(\подсхема_3_f2_3 [1]), .F2_3(\подсхема_3_f2_3 [0]), .F1_3(\подсхема_3_f0_3 [1]),
    .F0_3(\подсхема_3_f0_3 [0]));
  podshema4 \u_подсхема_4  (
    .x0_4(5'b00101), .F3_4(\подсхема_4_f2_4 [1]), .F2_4(\подсхема_4_f2_4 [0]), .F1_4(\подсхема_4_f0_4 [1]),
    .F0_4(\подсхема_4_f0_4 [0]));
  // Probe on \подсхема_1_f2_1 
  // Probe on \подсхема_1_f0_1 
  // Probe on \подсхема_2_f2_2 
  // Probe on \подсхема_2_f0_2 
  // Probe on \подсхема_3_f2_3 
  // Probe on \подсхема_3_f0_3 
  // Probe on \подсхема_4_f2_4 
  // Probe on \подсхема_4_f0_4 

  assign x0_4 = 5'b00101;

  // Notes on the sheet:
  //   Вход
endmodule

module podshema1 (
  input  [4:0] x0_4,
  output F3_1,
  output F2_1,
  output F1_1,
  output F0_1
);

  wire and_1_out, and_2_out, and_3_out, and_4_out, and_5_out, and_6_out, and_7_out, and_8_out, and_9_out,
       and_10_out, and_11_out, and_12_out, and_13_out, and_14_out, and_15_out, and_16_out, and_17_out,
       and_18_out, and_19_out, and_20_out, and_21_out, and_22_out, and_23_out, and_24_out, and_25_out,
       and_26_out, and_27_out, and_28_out, and_29_out, and_30_out, and_31_out, and_32_out, and_33_out,
       and_34_out, and_35_out, and_36_out, and_37_out, and_38_out, and_39_out, not_1_out, not_2_out,
       not_3_out, not_4_out, not_5_out, not_6_out, not_7_out, not_8_out, not_9_out, not_10_out, not_11_out,
       not_12_out, not_13_out, not_14_out, not_15_out, not_16_out, not_17_out, not_18_out, not_19_out,
       not_20_out, not_21_out, not_22_out, not_23_out, not_24_out, not_25_out, not_26_out, not_27_out,
       not_28_out, not_29_out, not_30_out, not_31_out, not_32_out, not_33_out, not_34_out, not_35_out,
       not_36_out, not_37_out, not_38_out, not_39_out, not_40_out, not_41_out, not_42_out, not_43_out,
       not_44_out, not_45_out, not_46_out, not_47_out, not_48_out, not_49_out, not_50_out, not_51_out,
       not_52_out, not_53_out, not_54_out, not_55_out, not_56_out, not_57_out, not_58_out, not_59_out,
       not_60_out, not_61_out, not_62_out, not_63_out, not_64_out, not_65_out, not_66_out, not_67_out,
       not_68_out, not_69_out, not_70_out, not_71_out, not_72_out, not_73_out, not_74_out, not_75_out,
       not_76_out, not_77_out, not_78_out, not_79_out, not_80_out, not_81_out, not_82_out, not_83_out,
       not_84_out, not_85_out, not_86_out, not_87_out, not_88_out, not_89_out, not_90_out;

  not not_1 (not_1_out, x0_4[4]);
  not not_2 (not_2_out, x0_4[2]);
  not not_3 (not_3_out, x0_4[4]);
  not not_4 (not_4_out, x0_4[0]);
  not not_5 (not_5_out, x0_4[2]);
  not not_6 (not_6_out, x0_4[0]);
  not not_7 (not_7_out, x0_4[4]);
  not not_8 (not_8_out, x0_4[1]);
  not not_9 (not_9_out, x0_4[3]);
  not not_10 (not_10_out, x0_4[1]);
  not not_11 (not_11_out, x0_4[3]);
  not not_12 (not_12_out, x0_4[0]);
  not not_13 (not_13_out, x0_4[4]);
  not not_14 (not_14_out, x0_4[3]);
  not not_15 (not_15_out, x0_4[0]);
  not not_16 (not_16_out, x0_4[3]);
  not not_17 (not_17_out, x0_4[2]);
  not not_18 (not_18_out, x0_4[0]);
  not not_19 (not_19_out, x0_4[4]);
  not not_20 (not_20_out, x0_4[3]);
  not not_21 (not_21_out, x0_4[1]);
  not not_22 (not_22_out, x0_4[4]);
  not not_23 (not_23_out, x0_4[2]);
  not not_24 (not_24_out, x0_4[1]);
  not not_25 (not_25_out, x0_4[4]);
  not not_26 (not_26_out, x0_4[2]);
  not not_27 (not_27_out, x0_4[0]);
  not not_28 (not_28_out, x0_4[4]);
  not not_29 (not_29_out, x0_4[1]);
  not not_30 (not_30_out, x0_4[0]);
  not not_31 (not_31_out, x0_4[4]);
  not not_32 (not_32_out, x0_4[3]);
  not not_33 (not_33_out, x0_4[1]);
  not not_34 (not_34_out, x0_4[0]);
  not not_35 (not_35_out, x0_4[3]);
  not not_36 (not_36_out, x0_4[2]);
  not not_37 (not_37_out, x0_4[1]);
  not not_38 (not_38_out, x0_4[0]);
  not not_39 (not_39_out, x0_4[4]);
  not not_40 (not_40_out, x0_4[3]);
  not not_41 (not_41_out, x0_4[2]);
  not not_42 (not_42_out, x0_4[0]);
  not not_43 (not_43_out, x0_4[4]);
  not not_44 (not_44_out, x0_4[3]);
  not not_45 (not_45_out, x0_4[1]);
  not not_46 (not_46_out, x0_4[4]);
  not not_47 (not_47_out, x0_4[2]);
  not not_48 (not_48_out, x0_4[1]);
  not not_49 (not_49_out, x0_4[0]);
  not not_50 (not_50_out, x0_4[4]);
  not not_51 (not_51_out, x0_4[2]);
  not not_52 (not_52_out, x0_4[4]);
  not not_53 (not_53_out, x0_4[0]);
  not not_54 (not_54_out, x0_4[3]);
  not not_55 (not_55_out, x0_4[2]);
  not not_56 (not_56_out, x0_4[1]);
  not not_57 (not_57_out, x0_4[3]);
  not not_58 (not_58_out, x0_4[1]);
  not not_59 (not_59_out, x0_4[0]);
  not not_60 (not_60_out, x0_4[3]);
  not not_61 (not_61_out, x0_4[2]);
  not not_62 (not_62_out, x0_4[0]);
  not not_63 (not_63_out, x0_4[1]);
  not not_64 (not_64_out, x0_4[4]);
  not not_65 (not_65_out, x0_4[3]);
  not not_66 (not_66_out, x0_4[2]);
  not not_67 (not_67_out, x0_4[1]);
  not not_68 (not_68_out, x0_4[4]);
  not not_69 (not_69_out, x0_4[3]);
  not not_70 (not_70_out, x0_4[1]);
  not not_71 (not_71_out, x0_4[0]);
  not not_72 (not_72_out, x0_4[4]);
  not not_73 (not_73_out, x0_4[3]);
  not not_74 (not_74_out, x0_4[4]);
  not not_75 (not_75_out, x0_4[2]);
  not not_76 (not_76_out, x0_4[0]);
  not not_77 (not_77_out, x0_4[4]);
  not not_78 (not_78_out, x0_4[1]);
  not not_79 (not_79_out, x0_4[3]);
  not not_80 (not_80_out, x0_4[2]);
  not not_81 (not_81_out, x0_4[1]);
  not not_82 (not_82_out, x0_4[0]);
  not not_83 (not_83_out, x0_4[3]);
  not not_84 (not_84_out, x0_4[2]);
  not not_85 (not_85_out, x0_4[3]);
  not not_86 (not_86_out, x0_4[0]);
  not not_87 (not_87_out, x0_4[2]);
  not not_88 (not_88_out, x0_4[1]);
  not not_89 (not_89_out, x0_4[1]);
  not not_90 (not_90_out, x0_4[0]);
  and and_1 (and_1_out, not_1_out, x0_4[3], not_2_out, x0_4[1]);
  and and_2 (and_2_out, not_3_out, x0_4[3], x0_4[1], not_4_out);
  and and_3 (and_3_out, x0_4[3], not_5_out, x0_4[1], not_6_out);
  and and_4 (and_4_out, not_7_out, x0_4[3], x0_4[2], not_8_out, x0_4[0]);
  and and_5 (and_5_out, x0_4[4], not_9_out, x0_4[2], not_10_out, x0_4[0]);
  and and_6 (and_6_out, x0_4[4], not_11_out, x0_4[2], x0_4[1], not_12_out);
  and and_7 (and_7_out, not_13_out, not_14_out, x0_4[1], not_15_out);
  and and_8 (and_8_out, not_16_out, not_17_out, x0_4[1], not_18_out);
  and and_9 (and_9_out, not_19_out, not_20_out, x0_4[2], not_21_out, x0_4[0]);
  and and_10 (and_10_out, not_22_out, x0_4[3], not_23_out, not_24_out);
  and and_11 (and_11_out, not_25_out, x0_4[3], not_26_out, not_27_out);
  and and_12 (and_12_out, not_28_out, x0_4[3], not_29_out, not_30_out);
  and and_13 (and_13_out, not_31_out, x0_4[3], x0_4[2], x0_4[1], x0_4[0]);
  and and_14 (and_14_out, x0_4[4], not_32_out, x0_4[2], not_33_out, not_34_out);
  and and_15 (and_15_out, x0_4[4], not_35_out, x0_4[2], x0_4[1], x0_4[0]);
  and and_16 (and_16_out, x0_4[4], x0_4[3], not_36_out, x0_4[1], x0_4[0]);
  and and_17 (and_17_out, x0_4[4], x0_4[3], x0_4[2], not_37_out, x0_4[0]);
  and and_18 (and_18_out, x0_4[4], x0_4[3], x0_4[2], x0_4[1], not_38_out);
  and and_19 (and_19_out, not_39_out, not_40_out, not_41_out, x0_4[1], not_42_out);
  and and_20 (and_20_out, not_43_out, not_44_out, x0_4[2], not_45_out, x0_4[0]);
  and and_21 (and_21_out, not_46_out, x0_4[3], not_47_out, not_48_out, not_49_out);
  and and_22 (and_22_out, not_50_out, x0_4[3], not_51_out, x0_4[1], x0_4[0]);
  and and_23 (and_23_out, not_52_out, x0_4[3], x0_4[2], x0_4[1], not_53_out);
  and and_24 (and_24_out, x0_4[4], not_54_out, not_55_out, not_56_out, x0_4[0]);
  and and_25 (and_25_out, x0_4[4], not_57_out, x0_4[2], not_58_out, not_59_out);
  and and_26 (and_26_out, x0_4[4], not_60_out, x0_4[2], x0_4[1], x0_4[0]);
  and and_27 (and_27_out, x0_4[4], x0_4[3], not_61_out, x0_4[1], not_62_out);
  and and_28 (and_28_out, x0_4[4], x0_4[3], x0_4[2], not_63_out, x0_4[0]);
  and and_29 (and_29_out, not_64_out, not_65_out, not_66_out, not_67_out, x0_4[0]);
  and and_30 (and_30_out, not_68_out, not_69_out, x0_4[2], not_70_out, not_71_out);
  and and_31 (and_31_out, not_72_out, not_73_out, x0_4[2], x0_4[1], x0_4[0]);
  and and_32 (and_32_out, not_74_out, x0_4[3], not_75_out, x0_4[1], not_76_out);
  and and_33 (and_33_out, not_77_out, x0_4[3], x0_4[2], not_78_out, x0_4[0]);
  and and_34 (and_34_out, x0_4[4], not_79_out, not_80_out, not_81_out, not_82_out);
  and and_35 (and_35_out, x0_4[4], not_83_out, not_84_out, x0_4[1], x0_4[0]);
  and and_36 (and_36_out, x0_4[4], not_85_out, x0_4[2], x0_4[1], not_86_out);
  and and_37 (and_37_out, x0_4[4], x0_4[3], not_87_out, not_88_out, x0_4[0]);
  and and_38 (and_38_out, x0_4[4], x0_4[3], x0_4[2], not_89_out, not_90_out);
  and and_39 (and_39_out, x0_4[4], x0_4[3], x0_4[2], x0_4[1], x0_4[0]);
  or or_1 (F3_1, and_1_out, and_2_out, and_3_out, and_4_out, and_5_out, and_6_out);
  or or_2 (F2_1, and_7_out, and_8_out, and_9_out, and_10_out, and_11_out, and_12_out, and_13_out, and_14_out, and_15_out, and_16_out, and_17_out, and_18_out);
  or or_3 (F1_1, and_19_out, and_20_out, and_21_out, and_22_out, and_23_out, and_24_out, and_25_out, and_26_out, and_27_out, and_28_out);
  or or_4 (F0_1, and_29_out, and_30_out, and_31_out, and_32_out, and_33_out, and_34_out, and_35_out, and_36_out, and_37_out, and_38_out, and_39_out);
endmodule

module podshema2 (
  input  [4:0] x0_4,
  output F3_2,
  output F2_2,
  output F1_2,
  output F0_2
);

  wire and_1_out, and_2_out, and_3_out, and_4_out, and_5_out, and_6_out, and_7_out, and_8_out, and_9_out,
       and_10_out, and_11_out, and_12_out, and_13_out, and_14_out, and_15_out, and_16_out, and_17_out,
       and_18_out, and_19_out, and_20_out, and_21_out, and_22_out, and_23_out, and_24_out, and_25_out,
       and_26_out, and_27_out, and_28_out, and_29_out, and_30_out, and_31_out, and_32_out, and_33_out,
       and_34_out, and_35_out, and_36_out, and_37_out, and_38_out, and_39_out, and_40_out, not_1_out,
       not_2_out, not_3_out, not_4_out, not_5_out, not_6_out, not_7_out, not_8_out, not_9_out, not_10_out,
       not_11_out, not_12_out, not_13_out, not_14_out, not_15_out, not_16_out, not_17_out, not_18_out,
       not_19_out, not_20_out, not_21_out, not_22_out, not_23_out, not_24_out, not_25_out, not_26_out,
       not_27_out, not_28_out, not_29_out, not_30_out, not_31_out, not_32_out, not_33_out, not_34_out,
       not_35_out, not_36_out, not_37_out, not_38_out, not_39_out, not_40_out, not_41_out, not_42_out,
       not_43_out, not_44_out, not_45_out, not_46_out, not_47_out, not_48_out, not_49_out, not_50_out,
       not_51_out, not_52_out, not_53_out, not_54_out, not_55_out, not_56_out, not_57_out, not_58_out,
       not_59_out, not_60_out, not_61_out, not_62_out, not_63_out, not_64_out, not_65_out, not_66_out,
       not_67_out, not_68_out, not_69_out, not_70_out, not_71_out, not_72_out, not_73_out, not_74_out,
       not_75_out, not_76_out, not_77_out, not_78_out, not_79_out, not_80_out, not_81_out, not_82_out,
       not_83_out;

  not not_1 (not_1_out, x0_4[4]);
  not not_2 (not_2_out, x0_4[2]);
  not not_3 (not_3_out, x0_4[4]);
  not not_4 (not_4_out, x0_4[0]);
  not not_5 (not_5_out, x0_4[2]);
  not not_6 (not_6_out, x0_4[0]);
  not not_7 (not_7_out, x0_4[4]);
  not not_8 (not_8_out, x0_4[1]);
  not not_9 (not_9_out, x0_4[3]);
  not not_10 (not_10_out, x0_4[1]);
  not not_11 (not_11_out, x0_4[3]);
  not not_12 (not_12_out, x0_4[0]);
  not not_13 (not_13_out, x0_4[4]);
  not not_14 (not_14_out, x0_4[2]);
  not not_15 (not_15_out, x0_4[0]);
  not not_16 (not_16_out, x0_4[4]);
  not not_17 (not_17_out, x0_4[3]);
  not not_18 (not_18_out, x0_4[0]);
  not not_19 (not_19_out, x0_4[3]);
  not not_20 (not_20_out, x0_4[2]);
  not not_21 (not_21_out, x0_4[0]);
  not not_22 (not_22_out, x0_4[4]);
  not not_23 (not_23_out, x0_4[3]);
  not not_24 (not_24_out, x0_4[1]);
  not not_25 (not_25_out, x0_4[4]);
  not not_26 (not_26_out, x0_4[2]);
  not not_27 (not_27_out, x0_4[1]);
  not not_28 (not_28_out, x0_4[4]);
  not not_29 (not_29_out, x0_4[1]);
  not not_30 (not_30_out, x0_4[0]);
  not not_31 (not_31_out, x0_4[3]);
  not not_32 (not_32_out, x0_4[1]);
  not not_33 (not_33_out, x0_4[0]);
  not not_34 (not_34_out, x0_4[4]);
  not not_35 (not_35_out, x0_4[3]);
  not not_36 (not_36_out, x0_4[2]);
  not not_37 (not_37_out, x0_4[0]);
  not not_38 (not_38_out, x0_4[4]);
  not not_39 (not_39_out, x0_4[2]);
  not not_40 (not_40_out, x0_4[1]);
  not not_41 (not_41_out, x0_4[0]);
  not not_42 (not_42_out, x0_4[4]);
  not not_43 (not_43_out, x0_4[3]);
  not not_44 (not_44_out, x0_4[1]);
  not not_45 (not_45_out, x0_4[4]);
  not not_46 (not_46_out, x0_4[2]);
  not not_47 (not_47_out, x0_4[4]);
  not not_48 (not_48_out, x0_4[0]);
  not not_49 (not_49_out, x0_4[3]);
  not not_50 (not_50_out, x0_4[2]);
  not not_51 (not_51_out, x0_4[1]);
  not not_52 (not_52_out, x0_4[3]);
  not not_53 (not_53_out, x0_4[1]);
  not not_54 (not_54_out, x0_4[0]);
  not not_55 (not_55_out, x0_4[2]);
  not not_56 (not_56_out, x0_4[0]);
  not not_57 (not_57_out, x0_4[4]);
  not not_58 (not_58_out, x0_4[3]);
  not not_59 (not_59_out, x0_4[2]);
  not not_60 (not_60_out, x0_4[1]);
  not not_61 (not_61_out, x0_4[4]);
  not not_62 (not_62_out, x0_4[3]);
  not not_63 (not_63_out, x0_4[1]);
  not not_64 (not_64_out, x0_4[0]);
  not not_65 (not_65_out, x0_4[3]);
  not not_66 (not_66_out, x0_4[2]);
  not not_67 (not_67_out, x0_4[1]);
  not not_68 (not_68_out, x0_4[0]);
  not not_69 (not_69_out, x0_4[4]);
  not not_70 (not_70_out, x0_4[3]);
  not not_71 (not_71_out, x0_4[4]);
  not not_72 (not_72_out, x0_4[2]);
  not not_73 (not_73_out, x0_4[0]);
  not not_74 (not_74_out, x0_4[4]);
  not not_75 (not_75_out, x0_4[1]);
  not not_76 (not_76_out, x0_4[3]);
  not not_77 (not_77_out, x0_4[2]);
  not not_78 (not_78_out, x0_4[3]);
  not not_79 (not_79_out, x0_4[0]);
  not not_80 (not_80_out, x0_4[2]);
  not not_81 (not_81_out, x0_4[1]);
  not not_82 (not_82_out, x0_4[1]);
  not not_83 (not_83_out, x0_4[0]);
  and and_1 (and_1_out, not_1_out, x0_4[3], not_2_out, x0_4[1]);
  and and_2 (and_2_out, not_3_out, x0_4[3], x0_4[1], not_4_out);
  and and_3 (and_3_out, x0_4[3], not_5_out, x0_4[1], not_6_out);
  and and_4 (and_4_out, not_7_out, x0_4[3], x0_4[2], not_8_out, x0_4[0]);
  and and_5 (and_5_out, x0_4[4], not_9_out, x0_4[2], not_10_out, x0_4[0]);
  and and_6 (and_6_out, x0_4[4], not_11_out, x0_4[2], x0_4[1], not_12_out);
  and and_7 (and_7_out, x0_4[4], x0_4[3], x0_4[2], x0_4[1], x0_4[0]);
  and and_8 (and_8_out, not_13_out, not_14_out, not_15_out);
  and and_9 (and_9_out, not_16_out, not_17_out, x0_4[1], not_18_out);
  and and_10 (and_10_out, not_19_out, not_20_out, x0_4[1], not_21_out);
  and and_11 (and_11_out, not_22_out, not_23_out, x0_4[2], not_24_out, x0_4[0]);
  and and_12 (and_12_out, not_25_out, x0_4[3], not_26_out, not_27_out);
  and and_13 (and_13_out, not_28_out, x0_4[3], not_29_out, not_30_out);
  and and_14 (and_14_out, x0_4[3], x0_4[2], x0_4[1], x0_4[0]);
  and and_15 (and_15_out, x0_4[4], not_31_out, x0_4[2], not_32_out, not_33_out);
  and and_16 (and_16_out, x0_4[4], x0_4[2], x0_4[1], x0_4[0]);
  and and_17 (and_17_out, x0_4[4], x0_4[3], x0_4[1], x0_4[0]);
  and and_18 (and_18_out, x0_4[4], x0_4[3], x0_4[2], x0_4[0]);
  and and_19 (and_19_out, x0_4[4], x0_4[3], x0_4[2], x0_4[1]);
  and and_20 (and_20_out, not_34_out, not_35_out, not_36_out, not_37_out);
  and and_21 (and_21_out, not_38_out, not_39_out, not_40_out, not_41_out);
  and and_22 (and_22_out, not_42_out, not_43_out, x0_4[2], not_44_out, x0_4[0]);
  and and_23 (and_23_out, not_45_out, x0_4[3], not_46_out, x0_4[1], x0_4[0]);
  and and_24 (and_24_out, not_47_out, x0_4[3], x0_4[2], x0_4[1], not_48_out);
  and and_25 (and_25_out, x0_4[4], not_49_out, not_50_out, not_51_out, x0_4[0]);
  and and_26 (and_26_out, x0_4[4], not_52_out, x0_4[2], not_53_out, not_54_out);
  and and_27 (and_27_out, x0_4[4], x0_4[2], x0_4[1], x0_4[0]);
  and and_28 (and_28_out, x0_4[4], x0_4[3], not_55_out, x0_4[1], not_56_out);
  and and_29 (and_29_out, x0_4[4], x0_4[3], x0_4[2], x0_4[0]);
  and and_30 (and_30_out, not_57_out, not_58_out, not_59_out, not_60_out);
  and and_31 (and_31_out, not_61_out, not_62_out, not_63_out, not_64_out);
  and and_32 (and_32_out, not_65_out, not_66_out, not_67_out, not_68_out);
  and and_33 (and_33_out, not_69_out, not_70_out, x0_4[2], x0_4[1], x0_4[0]);
  and and_34 (and_34_out, not_71_out, x0_4[3], not_72_out, x0_4[1], not_73_out);
  and and_35 (and_35_out, not_74_out, x0_4[3], x0_4[2], not_75_out, x0_4[0]);
  and and_36 (and_36_out, x0_4[4], not_76_out, not_77_out, x0_4[1], x0_4[0]);
  and and_37 (and_37_out, x0_4[4], not_78_out, x0_4[2], x0_4[1], not_79_out);
  and and_38 (and_38_out, x0_4[4], x0_4[3], not_80_out, not_81_out, x0_4[0]);
  and and_39 (and_39_out, x0_4[4], x0_4[3], x0_4[2], not_82_out, not_83_out);
  and and_40 (and_40_out, x0_4[4], x0_4[3], x0_4[2], x0_4[1], x0_4[0]);
  or or_1 (F3_2, and_1_out, and_2_out, and_3_out, and_4_out, and_5_out, and_6_out, and_7_out);
  or or_2 (F1_2, and_20_out, and_21_out, and_22_out, and_23_out, and_24_out, and_25_out, and_26_out, and_27_out, and_28_out, and_29_out);
  or or_3 (F0_2, and_30_out, and_31_out, and_32_out, and_33_out, and_34_out, and_35_out, and_36_out, and_37_out, and_38_out, and_39_out, and_40_out);
  or or_4 (F2_2, and_8_out, and_9_out, and_10_out, and_11_out, and_12_out, and_13_out, and_14_out, and_15_out, and_16_out, and_17_out, and_18_out, and_19_out);
endmodule

module podshema3 (
  input  [4:0] x0_4,
  output F3_3,
  output F2_3,
  output F1_3,
  output F0_3
);

  wire and_1_out, and_2_out, and_3_out, and_4_out, and_5_out, and_6_out, and_7_out, and_8_out, and_9_out,
       and_10_out, and_11_out, and_12_out, and_13_out, and_14_out, and_15_out, and_16_out, and_17_out,
       and_18_out, and_19_out, and_20_out, and_21_out, and_22_out, and_23_out, and_24_out, and_25_out,
       and_26_out, and_27_out, and_28_out, and_29_out, and_30_out, and_31_out, and_32_out, and_33_out,
       and_34_out, and_35_out, and_36_out, and_37_out, and_38_out, and_39_out, and_40_out, not_1_out,
       not_2_out, not_3_out, not_4_out, not_5_out, not_6_out, not_7_out, not_8_out, not_9_out, not_10_out,
       not_11_out, not_12_out, not_13_out, not_14_out, not_15_out, not_16_out, not_17_out, not_18_out,
       not_19_out, not_20_out, not_21_out, not_22_out, not_23_out, not_24_out, not_25_out, not_26_out,
       not_27_out, not_28_out, not_29_out, not_30_out, not_31_out, not_32_out, not_33_out, not_34_out,
       not_35_out, not_36_out, not_37_out, not_38_out, not_39_out, not_40_out, not_41_out, not_42_out,
       not_43_out, not_44_out, not_45_out, not_46_out, not_47_out, not_48_out, not_49_out, not_50_out,
       not_51_out, not_52_out, not_53_out, not_54_out, not_55_out, not_56_out, not_57_out, not_58_out,
       not_59_out, not_60_out, not_61_out, not_62_out, not_63_out, not_64_out, not_65_out, not_66_out,
       not_67_out, not_68_out, not_69_out, not_70_out, not_71_out, not_72_out, not_73_out, not_74_out,
       not_75_out, not_76_out, not_77_out, not_78_out, not_79_out, not_80_out, not_81_out, not_82_out,
       not_83_out, not_84_out, not_85_out, not_86_out, not_87_out, not_88_out, not_89_out, not_90_out,
       not_91_out, not_92_out, not_93_out;

  not not_1 (not_1_out, x0_4[3]);
  not not_2 (not_2_out, x0_4[1]);
  not not_3 (not_3_out, x0_4[2]);
  not not_4 (not_4_out, x0_4[0]);
  not not_5 (not_5_out, x0_4[4]);
  not not_6 (not_6_out, x0_4[2]);
  not not_7 (not_7_out, x0_4[4]);
  not not_8 (not_8_out, x0_4[0]);
  not not_9 (not_9_out, x0_4[3]);
  not not_10 (not_10_out, x0_4[0]);
  not not_11 (not_11_out, x0_4[4]);
  not not_12 (not_12_out, x0_4[1]);
  not not_13 (not_13_out, x0_4[4]);
  not not_14 (not_14_out, x0_4[2]);
  not not_15 (not_15_out, x0_4[0]);
  not not_16 (not_16_out, x0_4[2]);
  not not_17 (not_17_out, x0_4[0]);
  not not_18 (not_18_out, x0_4[4]);
  not not_19 (not_19_out, x0_4[3]);
  not not_20 (not_20_out, x0_4[1]);
  not not_21 (not_21_out, x0_4[0]);
  not not_22 (not_22_out, x0_4[4]);
  not not_23 (not_23_out, x0_4[3]);
  not not_24 (not_24_out, x0_4[1]);
  not not_25 (not_25_out, x0_4[1]);
  not not_26 (not_26_out, x0_4[3]);
  not not_27 (not_27_out, x0_4[3]);
  not not_28 (not_28_out, x0_4[2]);
  not not_29 (not_29_out, x0_4[0]);
  not not_30 (not_30_out, x0_4[4]);
  not not_31 (not_31_out, x0_4[2]);
  not not_32 (not_32_out, x0_4[1]);
  not not_33 (not_33_out, x0_4[4]);
  not not_34 (not_34_out, x0_4[1]);
  not not_35 (not_35_out, x0_4[0]);
  not not_36 (not_36_out, x0_4[4]);
  not not_37 (not_37_out, x0_4[3]);
  not not_38 (not_38_out, x0_4[0]);
  not not_39 (not_39_out, x0_4[4]);
  not not_40 (not_40_out, x0_4[2]);
  not not_41 (not_41_out, x0_4[0]);
  not not_42 (not_42_out, x0_4[3]);
  not not_43 (not_43_out, x0_4[2]);
  not not_44 (not_44_out, x0_4[1]);
  not not_45 (not_45_out, x0_4[4]);
  not not_46 (not_46_out, x0_4[2]);
  not not_47 (not_47_out, x0_4[1]);
  not not_48 (not_48_out, x0_4[0]);
  not not_49 (not_49_out, x0_4[4]);
  not not_50 (not_50_out, x0_4[3]);
  not not_51 (not_51_out, x0_4[2]);
  not not_52 (not_52_out, x0_4[0]);
  not not_53 (not_53_out, x0_4[2]);
  not not_54 (not_54_out, x0_4[0]);
  not not_55 (not_55_out, x0_4[4]);
  not not_56 (not_56_out, x0_4[2]);
  not not_57 (not_57_out, x0_4[4]);
  not not_58 (not_58_out, x0_4[0]);
  not not_59 (not_59_out, x0_4[3]);
  not not_60 (not_60_out, x0_4[1]);
  not not_61 (not_61_out, x0_4[0]);
  not not_62 (not_62_out, x0_4[4]);
  not not_63 (not_63_out, x0_4[3]);
  not not_64 (not_64_out, x0_4[1]);
  not not_65 (not_65_out, x0_4[1]);
  not not_66 (not_66_out, x0_4[3]);
  not not_67 (not_67_out, x0_4[3]);
  not not_68 (not_68_out, x0_4[2]);
  not not_69 (not_69_out, x0_4[1]);
  not not_70 (not_70_out, x0_4[0]);
  not not_71 (not_71_out, x0_4[4]);
  not not_72 (not_72_out, x0_4[3]);
  not not_73 (not_73_out, x0_4[2]);
  not not_74 (not_74_out, x0_4[1]);
  not not_75 (not_75_out, x0_4[4]);
  not not_76 (not_76_out, x0_4[3]);
  not not_77 (not_77_out, x0_4[1]);
  not not_78 (not_78_out, x0_4[0]);
  not not_79 (not_79_out, x0_4[2]);
  not not_80 (not_80_out, x0_4[1]);
  not not_81 (not_81_out, x0_4[3]);
  not not_82 (not_82_out, x0_4[2]);
  not not_83 (not_83_out, x0_4[1]);
  not not_84 (not_84_out, x0_4[0]);
  not not_85 (not_85_out, x0_4[4]);
  not not_86 (not_86_out, x0_4[3]);
  not not_87 (not_87_out, x0_4[3]);
  not not_88 (not_88_out, x0_4[0]);
  not not_89 (not_89_out, x0_4[4]);
  not not_90 (not_90_out, x0_4[1]);
  not not_91 (not_91_out, x0_4[4]);
  not not_92 (not_92_out, x0_4[2]);
  not not_93 (not_93_out, x0_4[0]);
  and and_1 (and_1_out, x0_4[4], not_1_out, x0_4[2], not_2_out, x0_4[0]);
  and and_2 (and_2_out, x0_4[4], x0_4[3], not_3_out, x0_4[1], not_4_out);
  and and_3 (and_3_out, not_5_out, x0_4[3], not_6_out, x0_4[1], x0_4[0]);
  and and_4 (and_4_out, not_7_out, x0_4[3], x0_4[2], x0_4[1], not_8_out);
  and and_5 (and_5_out, x0_4[4], not_9_out, x0_4[2], x0_4[1], not_10_out);
  and and_6 (and_6_out, not_11_out, x0_4[3], x0_4[2], not_12_out, x0_4[0]);
  and and_7 (and_7_out, not_13_out, x0_4[3], not_14_out, x0_4[1], not_15_out);
  and and_8 (and_8_out, x0_4[4], x0_4[3], not_16_out, x0_4[1], x0_4[0]);
  and and_9 (and_9_out, x0_4[4], x0_4[3], x0_4[2], x0_4[1], not_17_out);
  and and_10 (and_10_out, not_18_out, x0_4[3], x0_4[2], x0_4[1], x0_4[0]);
  and and_11 (and_11_out, x0_4[4], not_19_out, x0_4[2], not_20_out, not_21_out);
  and and_12 (and_12_out, not_22_out, not_23_out, x0_4[2], not_24_out, x0_4[0]);
  and and_13 (and_13_out, x0_4[4], x0_4[3], x0_4[2], not_25_out, x0_4[0]);
  and and_14 (and_14_out, x0_4[4], not_26_out, x0_4[2], x0_4[1], x0_4[0]);
  and and_15 (and_15_out, not_27_out, not_28_out, x0_4[1], not_29_out);
  and and_16 (and_16_out, not_30_out, x0_4[3], not_31_out, not_32_out);
  and and_17 (and_17_out, not_33_out, x0_4[3], not_34_out, not_35_out);
  and and_18 (and_18_out, not_36_out, not_37_out, x0_4[1], not_38_out);
  and and_19 (and_19_out, not_39_out, x0_4[3], not_40_out, x0_4[1], not_41_out);
  and and_20 (and_20_out, x0_4[4], not_42_out, not_43_out, not_44_out, x0_4[0]);
  and and_21 (and_21_out, not_45_out, x0_4[3], not_46_out, not_47_out, not_48_out);
  and and_22 (and_22_out, not_49_out, not_50_out, not_51_out, x0_4[1], not_52_out);
  and and_23 (and_23_out, x0_4[4], x0_4[3], not_53_out, x0_4[1], not_54_out);
  and and_24 (and_24_out, not_55_out, x0_4[3], not_56_out, x0_4[1], x0_4[0]);
  and and_25 (and_25_out, not_57_out, x0_4[3], x0_4[2], x0_4[1], not_58_out);
  and and_26 (and_26_out, x0_4[4], not_59_out, x0_4[2], not_60_out, not_61_out);
  and and_27 (and_27_out, not_62_out, not_63_out, x0_4[2], not_64_out, x0_4[0]);
  and and_28 (and_28_out, x0_4[4], x0_4[3], x0_4[2], not_65_out, x0_4[0]);
  and and_29 (and_29_out, x0_4[4], not_66_out, x0_4[2], x0_4[1], x0_4[0]);
  and and_30 (and_30_out, x0_4[4], not_67_out, not_68_out, not_69_out, not_70_out);
  and and_31 (and_31_out, not_71_out, not_72_out, not_73_out, not_74_out, x0_4[0]);
  and and_32 (and_32_out, not_75_out, not_76_out, x0_4[2], not_77_out, not_78_out);
  and and_33 (and_33_out, x0_4[4], x0_4[3], not_79_out, not_80_out, x0_4[0]);
  and and_34 (and_34_out, x0_4[4], not_81_out, not_82_out, x0_4[1], x0_4[0]);
  and and_35 (and_35_out, x0_4[4], x0_4[3], x0_4[2], not_83_out, not_84_out);
  and and_36 (and_36_out, not_85_out, not_86_out, x0_4[2], x0_4[1], x0_4[0]);
  and and_37 (and_37_out, x0_4[4], x0_4[3], x0_4[2], x0_4[1], x0_4[0]);
  and and_38 (and_38_out, x0_4[4], not_87_out, x0_4[2], x0_4[1], not_88_out);
  and and_39 (and_39_out, not_89_out, x0_4[3], x0_4[2], not_90_out, x0_4[0]);
  and and_40 (and_40_out, not_91_out, x0_4[3], not_92_out, x0_4[1], not_93_out);
  or or_1 (F3_3, and_1_out, and_2_out, and_3_out, and_4_out, and_5_out, and_6_out, and_7_out);
  or or_2 (F2_3, and_8_out, and_9_out, and_10_out, and_11_out, and_12_out, and_13_out, and_14_out, and_15_out, and_16_out, and_17_out, and_18_out, and_19_out);
  or or_3 (F1_3, and_20_out, and_21_out, and_22_out, and_23_out, and_24_out, and_25_out, and_26_out, and_27_out, and_28_out, and_29_out);
  or or_4 (F0_3, and_30_out, and_31_out, and_32_out, and_33_out, and_34_out, and_35_out, and_36_out, and_37_out, and_38_out, and_39_out, and_40_out);
endmodule

module podshema4 (
  input  [4:0] x0_4,
  output F3_4,
  output F2_4,
  output F1_4,
  output F0_4
);

  wire and_1_out, and_2_out, and_3_out, and_4_out, and_5_out, and_6_out, and_7_out, and_8_out, and_9_out,
       and_10_out, and_11_out, and_12_out, and_13_out, and_14_out, and_15_out, and_16_out, and_17_out,
       and_18_out, and_19_out, and_20_out, and_21_out, and_22_out, and_23_out, and_24_out, and_25_out,
       and_26_out, and_27_out, and_28_out, and_29_out, and_30_out, and_31_out, and_32_out, and_33_out,
       and_34_out, and_35_out, and_36_out, and_37_out, and_38_out, and_39_out, not_1_out, not_2_out,
       not_3_out, not_4_out, not_5_out, not_6_out, not_7_out, not_8_out, not_9_out, not_10_out, not_11_out,
       not_12_out, not_13_out, not_14_out, not_15_out, not_16_out, not_17_out, not_18_out, not_19_out,
       not_20_out, not_21_out, not_22_out, not_23_out, not_24_out, not_25_out, not_26_out, not_27_out,
       not_28_out, not_29_out, not_30_out, not_31_out, not_32_out, not_33_out, not_34_out, not_35_out,
       not_36_out, not_37_out, not_38_out, not_39_out, not_40_out, not_41_out, not_42_out, not_43_out,
       not_44_out, not_45_out, not_46_out, not_47_out, not_48_out, not_49_out, not_50_out, not_51_out,
       not_52_out, not_53_out, not_54_out, not_55_out, not_56_out, not_57_out, not_58_out, not_59_out,
       not_60_out, not_61_out, not_62_out, not_63_out, not_64_out, not_65_out, not_66_out, not_67_out,
       not_68_out, not_69_out, not_70_out, not_71_out, not_72_out, not_73_out, not_74_out, not_75_out,
       not_76_out, not_77_out, not_78_out, not_79_out, not_80_out, not_81_out, not_82_out, not_83_out,
       not_84_out, not_85_out, not_86_out;

  not not_1 (not_1_out, x0_4[3]);
  not not_2 (not_2_out, x0_4[1]);
  not not_3 (not_3_out, x0_4[2]);
  not not_4 (not_4_out, x0_4[0]);
  not not_5 (not_5_out, x0_4[4]);
  not not_6 (not_6_out, x0_4[2]);
  not not_7 (not_7_out, x0_4[3]);
  not not_8 (not_8_out, x0_4[0]);
  not not_9 (not_9_out, x0_4[4]);
  not not_10 (not_10_out, x0_4[1]);
  not not_11 (not_11_out, x0_4[4]);
  not not_12 (not_12_out, x0_4[0]);
  not not_13 (not_13_out, x0_4[4]);
  not not_14 (not_14_out, x0_4[2]);
  not not_15 (not_15_out, x0_4[0]);
  not not_16 (not_16_out, x0_4[3]);
  not not_17 (not_17_out, x0_4[1]);
  not not_18 (not_18_out, x0_4[0]);
  not not_19 (not_19_out, x0_4[4]);
  not not_20 (not_20_out, x0_4[3]);
  not not_21 (not_21_out, x0_4[1]);
  not not_22 (not_22_out, x0_4[3]);
  not not_23 (not_23_out, x0_4[2]);
  not not_24 (not_24_out, x0_4[0]);
  not not_25 (not_25_out, x0_4[4]);
  not not_26 (not_26_out, x0_4[2]);
  not not_27 (not_27_out, x0_4[1]);
  not not_28 (not_28_out, x0_4[4]);
  not not_29 (not_29_out, x0_4[1]);
  not not_30 (not_30_out, x0_4[0]);
  not not_31 (not_31_out, x0_4[4]);
  not not_32 (not_32_out, x0_4[3]);
  not not_33 (not_33_out, x0_4[0]);
  not not_34 (not_34_out, x0_4[4]);
  not not_35 (not_35_out, x0_4[2]);
  not not_36 (not_36_out, x0_4[0]);
  not not_37 (not_37_out, x0_4[3]);
  not not_38 (not_38_out, x0_4[2]);
  not not_39 (not_39_out, x0_4[1]);
  not not_40 (not_40_out, x0_4[2]);
  not not_41 (not_41_out, x0_4[0]);
  not not_42 (not_42_out, x0_4[4]);
  not not_43 (not_43_out, x0_4[2]);
  not not_44 (not_44_out, x0_4[4]);
  not not_45 (not_45_out, x0_4[0]);
  not not_46 (not_46_out, x0_4[3]);
  not not_47 (not_47_out, x0_4[1]);
  not not_48 (not_48_out, x0_4[0]);
  not not_49 (not_49_out, x0_4[4]);
  not not_50 (not_50_out, x0_4[3]);
  not not_51 (not_51_out, x0_4[1]);
  not not_52 (not_52_out, x0_4[4]);
  not not_53 (not_53_out, x0_4[2]);
  not not_54 (not_54_out, x0_4[1]);
  not not_55 (not_55_out, x0_4[0]);
  not not_56 (not_56_out, x0_4[4]);
  not not_57 (not_57_out, x0_4[3]);
  not not_58 (not_58_out, x0_4[2]);
  not not_59 (not_59_out, x0_4[0]);
  not not_60 (not_60_out, x0_4[2]);
  not not_61 (not_61_out, x0_4[1]);
  not not_62 (not_62_out, x0_4[3]);
  not not_63 (not_63_out, x0_4[2]);
  not not_64 (not_64_out, x0_4[1]);
  not not_65 (not_65_out, x0_4[0]);
  not not_66 (not_66_out, x0_4[4]);
  not not_67 (not_67_out, x0_4[3]);
  not not_68 (not_68_out, x0_4[3]);
  not not_69 (not_69_out, x0_4[0]);
  not not_70 (not_70_out, x0_4[4]);
  not not_71 (not_71_out, x0_4[1]);
  not not_72 (not_72_out, x0_4[3]);
  not not_73 (not_73_out, x0_4[2]);
  not not_74 (not_74_out, x0_4[1]);
  not not_75 (not_75_out, x0_4[0]);
  not not_76 (not_76_out, x0_4[4]);
  not not_77 (not_77_out, x0_4[3]);
  not not_78 (not_78_out, x0_4[2]);
  not not_79 (not_79_out, x0_4[1]);
  not not_80 (not_80_out, x0_4[4]);
  not not_81 (not_81_out, x0_4[3]);
  not not_82 (not_82_out, x0_4[1]);
  not not_83 (not_83_out, x0_4[0]);
  not not_84 (not_84_out, x0_4[4]);
  not not_85 (not_85_out, x0_4[2]);
  not not_86 (not_86_out, x0_4[0]);
  and and_1 (and_1_out, x0_4[4], not_1_out, x0_4[2], not_2_out, x0_4[0]);
  and and_2 (and_2_out, x0_4[4], x0_4[3], not_3_out, x0_4[1], not_4_out);
  and and_3 (and_3_out, not_5_out, x0_4[3], not_6_out, x0_4[1], x0_4[0]);
  and and_4 (and_4_out, x0_4[4], not_7_out, x0_4[2], x0_4[1], not_8_out);
  and and_5 (and_5_out, not_9_out, x0_4[3], x0_4[2], not_10_out, x0_4[0]);
  and and_6 (and_6_out, not_11_out, x0_4[3], x0_4[2], x0_4[1], not_12_out);
  and and_7 (and_7_out, not_13_out, x0_4[3], not_14_out, x0_4[1], not_15_out);
  and and_8 (and_8_out, x0_4[4], not_16_out, x0_4[2], not_17_out, not_18_out);
  and and_9 (and_9_out, not_19_out, not_20_out, x0_4[2], not_21_out, x0_4[0]);
  and and_10 (and_10_out, x0_4[3], x0_4[2], x0_4[1], x0_4[0]);
  and and_11 (and_11_out, x0_4[4], x0_4[3], x0_4[1], x0_4[0]);
  and and_12 (and_12_out, x0_4[4], x0_4[3], x0_4[2], x0_4[1]);
  and and_13 (and_13_out, not_22_out, not_23_out, x0_4[1], not_24_out);
  and and_14 (and_14_out, not_25_out, x0_4[3], not_26_out, not_27_out);
  and and_15 (and_15_out, not_28_out, x0_4[3], not_29_out, not_30_out);
  and and_16 (and_16_out, not_31_out, not_32_out, x0_4[1], not_33_out);
  and and_17 (and_17_out, not_34_out, x0_4[3], not_35_out, x0_4[1], not_36_out);
  and and_18 (and_18_out, x0_4[4], x0_4[2], x0_4[1], x0_4[0]);
  and and_19 (and_19_out, x0_4[4], x0_4[3], x0_4[2], x0_4[0]);
  and and_20 (and_20_out, x0_4[4], not_37_out, not_38_out, not_39_out, x0_4[0]);
  and and_21 (and_21_out, x0_4[4], x0_4[3], not_40_out, x0_4[1], not_41_out);
  and and_22 (and_22_out, not_42_out, x0_4[3], not_43_out, x0_4[1], x0_4[0]);
  and and_23 (and_23_out, not_44_out, x0_4[3], x0_4[2], x0_4[1], not_45_out);
  and and_24 (and_24_out, x0_4[4], not_46_out, x0_4[2], not_47_out, not_48_out);
  and and_25 (and_25_out, not_49_out, not_50_out, x0_4[2], not_51_out, x0_4[0]);
  and and_26 (and_26_out, not_52_out, not_53_out, not_54_out, not_55_out);
  and and_27 (and_27_out, not_56_out, not_57_out, not_58_out, not_59_out);
  and and_28 (and_28_out, x0_4[4], x0_4[2], x0_4[1], x0_4[0]);
  and and_29 (and_29_out, x0_4[4], x0_4[3], x0_4[2], x0_4[0]);
  and and_30 (and_30_out, x0_4[4], x0_4[3], not_60_out, not_61_out, x0_4[0]);
  and and_31 (and_31_out, x0_4[4], not_62_out, not_63_out, x0_4[1], x0_4[0]);
  and and_32 (and_32_out, x0_4[4], x0_4[3], x0_4[2], not_64_out, not_65_out);
  and and_33 (and_33_out, not_66_out, not_67_out, x0_4[2], x0_4[1], x0_4[0]);
  and and_34 (and_34_out, x0_4[4], not_68_out, x0_4[2], x0_4[1], not_69_out);
  and and_35 (and_35_out, not_70_out, x0_4[3], x0_4[2], not_71_out, x0_4[0]);
  and and_36 (and_36_out, not_72_out, not_73_out, not_74_out, not_75_out);
  and and_37 (and_37_out, not_76_out, not_77_out, not_78_out, not_79_out);
  and and_38 (and_38_out, not_80_out, not_81_out, not_82_out, not_83_out);
  and and_39 (and_39_out, not_84_out, x0_4[3], not_85_out, x0_4[1], not_86_out);
  or or_1 (F3_4, and_1_out, and_2_out, and_3_out, and_4_out, and_5_out, and_6_out, and_7_out);
  or or_2 (F2_4, and_8_out, and_9_out, and_10_out, and_11_out, and_12_out, and_13_out, and_14_out, and_15_out, and_16_out, and_17_out, and_18_out, and_19_out);
  or or_3 (F1_4, and_20_out, and_21_out, and_22_out, and_23_out, and_24_out, and_25_out, and_26_out, and_27_out, and_28_out, and_29_out);
  or or_4 (F0_4, and_30_out, and_31_out, and_32_out, and_33_out, and_34_out, and_35_out, and_36_out, and_37_out, and_38_out, and_39_out);
endmodule
