// Logisim project лаб4.circ as structural Verilog
module \Асинхронный_RS  (
  input  R,
  input  S,
  output Q1,
  output nQ1
);

  nor nor_1 (Q1, R, nQ1);
  nor nor_2 (nQ1, Q1, S);
endmodule

module \Асинхронный_RS_инв  (
  input  nS,
  input  nR
);

  wire nand_1_out, nand_2_out;

  nand nand_1 (nand_1_out, nS, nand_2_out);
  nand nand_2 (nand_2_out, nand_1_out, nR);
  // Probe on nand_1_out
  // Probe on nand_2_out
endmodule

module \Синхронный_RS  (
  input  S,
  input  C,
  input  R
);

  wire nand_1_out, nand_2_out, nand_3_out, nand_4_out;

  nand nand_1 (nand_1_out, S, C);
  nand nand_2 (nand_2_out, C, R);
  nand nand_3 (nand_3_out, nand_1_out, nand_4_out);
  nand nand_4 (nand_4_out, nand_3_out, nand_2_out);
  // Probe on nand_3_out
  // Probe on nand_4_out
endmodule

module \S_триггер  (
  input  S,
  input  R,
  output Q3,
  output nQ3
);

  wire nand_1_out, nand_2_out;

  nand nand_1 (nand_1_out, S, S);
  nand nand_2 (nand_2_out, nand_1_out, R);
  nand nand_3 (Q3, nand_1_out, nQ3);
  nand nand_4 (nQ3, Q3, nand_2_out);
endmodule

module \R_триггер  (
  input  S,
  input  R
);

  wire nand_1_out, nand_2_out, nand_3_out, nand_4_out;

  nand nand_1 (nand_1_out, S, nand_2_out);
  nand nand_2 (nand_2_out, R, R);
  nand nand_3 (nand_3_out, nand_1_out, nand_4_out);
  nand nand_4 (nand_4_out, nand_3_out, nand_2_out);
  // Probe on nand_3_out
  // Probe on nand_4_out

  // Notes on the sheet:
  //   R-триггер
endmodule

module \E_триггер  (
  input  S,
  input  R
);

  wire nand_1_out, nand_2_out, nand_3_out, nand_4_out, nand_5_out, nand_6_out;

  nand nand_1 (nand_1_out, S, S);
  nand nand_2 (nand_2_out, R, R);
  nand nand_3 (nand_3_out, S, nand_2_out);
  nand nand_4 (nand_4_out, nand_1_out, R);
  nand nand_5 (nand_5_out, nand_3_out, nand_6_out);
  nand nand_6 (nand_6_out, nand_5_out, nand_4_out);
  // Probe on nand_5_out
  // Probe on nand_6_out
endmodule
