// Logisim project лаб5.circ as structural Verilog
module \D_триггер  (
  input  D,
  input  C
);

  wire nand_1_out, nand_2_out, nand_3_out, nand_4_out;

  nand nand_1 (nand_1_out, D, C);
  nand nand_2 (nand_2_out, nand_1_out, C);
  nand nand_3 (nand_3_out, nand_1_out, nand_4_out);
  nand nand_4 (nand_4_out, nand_3_out, nand_2_out);
  // Probe on nand_3_out
  // Probe on nand_4_out

  // Notes on the sheet:
  //   D-триггер
endmodule

module \T_триггер  (
  input  T,
  input  C
);

  wire d_ff_1_q, d_ff_1_qn, nand_1_out;

  nand nand_1 (nand_1_out, T, C);
  D_Flip_Flop d_ff_1 (.clk(nand_1_out), .D(d_ff_1_qn), .Q(d_ff_1_q), .Qn(d_ff_1_qn));  // open: preset, en, reset
  // Probe on d_ff_1_q
  // Probe on d_ff_1_qn

  // Notes on the sheet:
  //   T-триггер
endmodule

module \JK_триггер  (
  input  J,
  input  C,
  input  K
);

  wire nand_1_out, nand_2_out, nand_3_out, nand_4_out, nand_5_out, nand_6_out, nand_7_out, nand_8_out;

  nand nand_1 (nand_1_out, nand_8_out, J, C);
  nand nand_2 (nand_2_out, C, K, nand_7_out);
  nand nand_3 (nand_3_out, nand_1_out, nand_4_out);
  nand nand_4 (nand_4_out, nand_3_out, nand_2_out);
  nand nand_5 (nand_5_out, nand_1_out, nand_3_out);
  nand nand_6 (nand_6_out, nand_4_out, nand_2_out);
  nand nand_7 (nand_7_out, nand_5_out, nand_8_out);
  nand nand_8 (nand_8_out, nand_7_out, nand_6_out);
  // Probe on nand_7_out
  // Probe on nand_8_out
endmodule
