// Logisim project lab6.circ as structural Verilog: 7 circuits, main circuit main
module main (
);
endmodule

module \полусумматор  (
  input  X1,
  input  X2,
  output P,
  output S
);

  and and_1 (P, X1, X2);
  \Схема_сравнения  \u_схема_сравнения_1  (.X1(X1), .X2(X2), .Y(S));

  // Notes on the sheet:
  //   Полусумматор
  //   Старший разряд - перенос
  //   Младший разряд
endmodule

module \Схема_сравнения  (
  input  X1,
  input  X2,
  output Y
);

  wire and_1_out, and_2_out, not_1_out, not_2_out;

  not not_1 (not_1_out, X1);
  not not_2 (not_2_out, X2);
  and and_1 (and_1_out, not_1_out, X2);
  and and_2 (and_2_out, X1, not_2_out);
  xor xor_1 (Y, and_1_out, and_2_out);

  // Notes on the sheet:
  //   схема сравнения
endmodule

module \сумматор  (
  input  X1,
  input  X2,
  input  Pi,
  output P,
  output S
);

  wire \Полусумматор_2_p , \Полусумматор_p , \Полусумматор_s ;

  \полусумматор  \u_Полусумматор  (.X1(X1), .X2(X2), .P(\Полусумматор_p ), .S(\Полусумматор_s ));
  \полусумматор  \u_Полусумматор_2  (.X1(\Полусумматор_s ), .X2(Pi), .P(\Полусумматор_2_p ), .S(S));
  xor xor_1 (P, \Полусумматор_p , \Полусумматор_2_p );

  // Notes on the sheet:
  //   перенос из предыдущего разряда
  //   Перенос
  //   Младший разряд суммы
endmodule

module \сумматор_4_х_разрядный  (
  input  X4,
  input  Y4,
  input  X3,
  input  Y3,
  input  X2,
  input  Y2,
  input  X1,
  input  Y1,
  input  Pi,
  output P,
  output S4,
  output S3,
  output S2,
  output S1
);

  wire \сумматор_1_p , \сумматор_2_p , \сумматор_3_p ;

  \сумматор  \u_сумматор_1  (.X1(X2), .X2(Y2), .Pi(\сумматор_2_p ), .P(\сумматор_1_p ), .S(S2));
  \сумматор  \u_сумматор_2  (.X1(X1), .X2(Y1), .Pi(Pi), .P(\сумматор_2_p ), .S(S1));
  \сумматор  \u_сумматор_3  (.X1(X3), .X2(Y3), .Pi(\сумматор_1_p ), .P(\сумматор_3_p ), .S(S3));
  \сумматор  \u_сумматор_4  (.X1(X4), .X2(Y4), .Pi(\сумматор_3_p ), .P(P), .S(S4));

  // Notes on the sheet:
  //   Схема 4-разрядного сумматора
  //   Перенос
endmodule

module \полусумматор_теория  (
  input  A,
  input  B,
  output S,
  output P
);

  wire not_1_out, or_1_out;

  or or_1 (or_1_out, A, B);
  and and_1 (P, A, B);
  not not_1 (not_1_out, P);
  and and_2 (S, or_1_out, not_1_out);

  // Notes on the sheet:
  //   Перенос
  //   Младший разряд суммы
endmodule

module \сумматор_теория  (
  input  A,
  input  B,
  input  P0,
  output P,
  output S
);

  wire and_1_out, and_2_out, and_3_out, and_4_out, and_5_out, not_1_out, or_1_out;

  and and_1 (and_1_out, A, B);
  and and_2 (and_2_out, A, P0);
  and and_3 (and_3_out, B, P0);
  or or_1 (or_1_out, A, B, P0);
  and and_4 (and_4_out, A, B, P0);
  or or_2 (P, and_1_out, and_2_out, and_3_out);
  not not_1 (not_1_out, P);
  and and_5 (and_5_out, not_1_out, or_1_out);
  or or_3 (S, and_5_out, and_4_out);

  // Notes on the sheet:
  //   Перенос
  //   Младший разряд суммы
endmodule
